# Fritzing sketch 01_schematic (saved by Fritzing 0.9.0b)
breadboards: 1

parts:
  Part1 = Arduino Uno (Rev3)
  LED1 = LED - 5mm [color="Red (633nm)" package="5 mm [THT]"]
  LED2 = LED - 5mm [color="Red (633nm)" package="5 mm [THT]"]
  LED3 = LED - 5mm [color="Red (633nm)" package="5 mm [THT]"]
  R1 = Resistor [tolerance=±5% resistance=100 package=THT]
  R2 = Resistor [tolerance=±5% resistance=100 package=THT]
  R3 = Resistor [tolerance=±5% resistance=100 package=THT]
  S2 = Pushbutton [package="[THT]"]
  R4 = Resistor [tolerance=±5% resistance=10k package=THT]
  R5 = TRIMPOT [package=trimpot-3mm-2]

nets:
  N1: Part1.A2, R5.WIPER
  N2: Part1.D8, S2.Pin_1, S2.Pin_2, R4.Pin_0
  N3: Part1.D11_PWM/MOSI, LED1.anode
  N4: Part1.D12/MISO, LED2.anode
  N5: Part1.D13/SCK, LED3.anode
  N6: Part1.5V, S2.Pin_3, S2.Pin_4, R5.CCW
  N7: Part1.GND, R1.Pin_1, R2.Pin_1, R3.Pin_1, R4.Pin_1, R5.CW
  N8: LED1.cathode, R1.Pin_0
  N9: LED2.cathode, R2.Pin_0
  N10: LED3.cathode, R3.Pin_0
